# Fritzing sketch digitdia_arduinoshield (saved by Fritzing 0.9.6b)
circuit board: 6.9215cm x 5.33756cm
breadboards: 1

parts:
  Poti1 = Trimmer Potentiometer [maximum_resistance=10kΩ package=THT]
  Poti2 = Trimmer Potentiometer [maximum_resistance=10kΩ package=THT]
  RL1 = Header 6 [package=molex-1x6_lock]
  RL2 = Header 6 [package=molex-1x6_lock]
  R1 = Resistor [tolerance=±5% resistance=470 power=0.25 package=THT]
  R2 = Resistor [tolerance=±5% resistance=470 power=0.25 package=THT]
  R4 = Resistor [tolerance=±5% resistance=1k power=0.25 package=THT]
  LED1 = LED - 3mm [color="Red (633nm)" current=0.030 package="3 mm [THT]"]
  LED2 = LED - 3mm [color="Red (633nm)" current=0.030 package="3 mm [THT]"]
  R3 = Resistor [tolerance=±5% resistance=1k power=0.25 package=THT]
  bang1 = Pushbutton [package="[THT]"]
  bang2 = Pushbutton [package="[THT]"]
  R6 = Resistor [tolerance=±5% resistance=1k power=0.25 package=THT]
  R5 = Resistor [tolerance=±5% resistance=1k power=0.25 package=THT]
  trans-port = screw terminal, 4 pins
  relay-port = screw terminal, 4 pins
  Part1 = Arduino Uno (Rev3)
  SW1 = DIP SWITCH [package=dipswitch-02]
  R7 = Resistor [tolerance=±5% resistance=220 power=0.25 package=THT]
  R8 = Resistor [tolerance=±5% resistance=220 power=0.25 package=THT]
  PNP01 = PNP-Transistor [package="TO92 [THT]"]
  PNP02 = PNP-Transistor [package="TO92 [THT]"]
  JP1 = Header 5x2 [package=2x5-ra]
  JP2 = Header 5x2 [package=2x5-ra]
  JP3 = Header 5x2 [package=2x5-ra]
  JP5 = Header 5x2 [package=2x5-ra]
  JP4 = Header 5x2 [package=2x5-ra]

nets:
  N1: Poti1.leg1, Poti2.leg1, RL1.4, RL2.4, R1.Pin_1, R2.Pin_1, R6.Pin_1, R5.Pin_1, trans-port.pin2, trans-port.pin4, Part1.GND, SW1.3, SW1.4, PNP01.C, PNP02.C
  N2: Poti1.wiper, Part1.A0
  N3: Poti1.leg2, Poti2.leg2, bang1.Pin_3, bang1.Pin_4, bang2.Pin_3, bang2.Pin_4, Part1.5V, R7.Pin_1, R8.Pin_1
  N4: Poti2.wiper, Part1.A1
  N5: RL1.1, relay-port.pin1
  N6: RL1.3, Part1.D8
  N7: RL1.6, relay-port.pin2
  N8: RL2.1, relay-port.pin3
  N9: RL2.3, Part1.D9_PWM
  N10: RL2.6, relay-port.pin4
  N11: R1.Pin_0, R3.Pin_0, PNP02.B
  N12: R2.Pin_0, R4.Pin_0, PNP01.B
  N13: R4.Pin_1, LED1.anode
  N14: LED1.cathode, Part1.D6_PWM
  N15: LED2.cathode, Part1.D5_PWM
  N16: LED2.anode, R3.Pin_1
  N17: bang1.Pin_1, bang1.Pin_2, R5.Pin_0, Part1.D3_PWM
  N18: bang2.Pin_1, bang2.Pin_2, R6.Pin_0, Part1.D4
  N19: trans-port.pin1, PNP01.E
  N20: trans-port.pin3, PNP02.E
  N21: Part1.D10_PWM/SS, SW1.2, R8.Pin_0
  N22: Part1.D11_PWM/MOSI, SW1.1, R7.Pin_0
  N23: JP1.1, JP1.2, JP2.1, JP2.2
  N24: JP1.3, JP1.4, JP2.3, JP2.4
  N25: JP1.5, JP1.6, JP2.5, JP2.6
  N26: JP1.7, JP1.8, JP2.7, JP2.8
  N27: JP1.9, JP1.10, JP2.9, JP2.10
  N28: JP3.1, JP3.2, JP4.1, JP4.2
  N29: JP3.3, JP3.4, JP4.3, JP4.4
  N30: JP3.5, JP3.6, JP4.5, JP4.6
  N31: JP3.7, JP3.8, JP4.7, JP4.8
  N32: JP3.9, JP3.10, JP4.9, JP4.10
  N33: JP5.1, JP5.2
  N34: JP5.3, JP5.4
  N35: JP5.5, JP5.6
  N36: JP5.7, JP5.8
  N37: JP5.9, JP5.10

notes:
  highly
  professional
  haushaltshilfe
  v1
  benjamin@lafkon.net

// code stored in the sketch: digitdia-code-001.ino

